# Fritzing sketch Stepper28BYJ48 (saved by Fritzing 0.9.3b)

parts:
  MOTOR1 = 28BYJ-48 Stepper Motor  # not connected
  X1 = X113647 Stepper Driver Board [package=board]
  pyboard1 = Micro Python pyboard [part_number=PYBv10b]

nets:
  N1: X1.IN1, pyboard1.X1
  N2: X1.IN2, pyboard1.X2
  N3: X1.IN3, pyboard1.X3
  N4: X1.IN4, pyboard1.X4
  N5: X1.GND, pyboard1.Y14_GND
  N6: X1.+V, pyboard1.Y16_VIN

custom parts:
  X113647 Stepper Driver Board: A common stepper motor driver board based on ULN2003APG darlington array
